# Fritzing sketch web2wire (saved by Fritzing 1.0.5)
breadboards: 1

parts:
  A1 = ESP32-S3-WROOM-1-N16R8 dev board
  M1 = lcd color display 0.96in 80x160 8pin interface [package=THT]

nets:
  N1: A1.Pin_1, A1.Pin_2, M1.VCC, M1.BLK
  N2: A1.Pin_4, M1.RES
  N3: A1.Pin_5, M1.CS
  N4: A1.Pin_6, M1.DC
  N5: A1.Pin_22, M1.GND
  N6: A1.Pin_32, M1.SDA
  N7: A1.Pin_33, M1.SCL

custom parts:
  ESP32-S3-WROOM-1-N16R8 dev board: ESP32-S3 WIFI+BLE5.0 Development Board ESP32-S3-WROOM-1-N16R8(16M Flash/8SRAM).
  lcd color display 0.96in 80x160 8pin interface: Ips 0.96 Inch 8 Pin Spi Hd 65K Full Color Tft Module St7735 Drive Ic 80 x 160 Lcd Display 3.3V Spi Interface.
